# Fritzing sketch Auxiliary Board (saved by Fritzing 0.9.3b)
circuit board: 12cm x 8cm
perfboards: 1

parts:
  Arduino_Nano_1 = Arduino Nano (Rev3.0)
  Steer_Servo_RR = male pin header, 3 pins [form="♂ (male)"]
  Steer_Servo_RL = male pin header, 3 pins [form="♂ (male)"]
  Motor_Driver_Rear = Motor Driver 1A Dual TB6612FNG
  Motor_Driver_Front = Motor Driver 1A Dual TB6612FNG
  Arduino_Nano_2 = Arduino Nano (Rev3.0)
  Drive_Motor_FR = Screw terminal - 2 pins [package=THT]
  Drive_Motor_FL = Screw terminal - 2 pins [package=THT]
  Drive_Motor_RL = Screw terminal - 2 pins [package=THT]
  Drive_Motor_RR = Screw terminal - 2 pins [package=THT]
  Steer_Servo_FL = male pin header, 3 pins [form="♂ (male)"]
  MPU9250 = female pin header, 10 pins [form="♀ (female)"]
  LED_GND = male pin header, 4 pins [form="♂ (male)"]
  Encoder_Power = male pin header, 4 pins [form="♂ (male)"]
  RL_Encoder_1 = male pin header, 1 pin [form="♂ (male)"]
  RL_Encoder_2 = male pin header, 1 pin [form="♂ (male)"]
  RR_Encoder_1 = male pin header, 1 pin [form="♂ (male)"]
  RR_Encoder_2 = male pin header, 1 pin [form="♂ (male)"]
  FL_Encoder_1 = male pin header, 1 pin [form="♂ (male)"]
  FL_Encoder_2 = male pin header, 1 pin [form="♂ (male)"]
  FR_Encoder_2 = male pin header, 1 pin [form="♂ (male)"]
  FR_Encoder_1 = male pin header, 1 pin [form="♂ (male)"]
  Taillights = male pin header, 2 pins [form="♂ (male)"]
  Headlights_(High_Beam) = male pin header, 2 pins [form="♂ (male)"]
  Headlights_(Low_Beam) = male pin header, 2 pins [form="♂ (male)"]
  Reverse_Indicators = male pin header, 2 pins [form="♂ (male)"]
  Left_Indicators = male pin header, 2 pins [form="♂ (male)"]
  Right_Indicators = male pin header, 2 pins [form="♂ (male)"]
  SBC_Power = Screw terminal - 2 pins [package=THT]
  Switch = Screw terminal - 2 pins [package=THT]
  Steer_Servo_FR = male pin header, 3 pins [form="♂ (male)"]
  Buzzer = Buzzer 12mm [package=buzzer-12mm-ns]
  Microphone_Power = male pin header, 2 pins [form="♂ (male)"]
  Microphone = male pin header, 2 pins [form="♂ (male)"]

nets:
  GND: Arduino_Nano_1.GND, Steer_Servo_RR.pin3, Steer_Servo_RL.pin3, Motor_Driver_Rear.GND, Motor_Driver_Front.GND, Arduino_Nano_2.GND, Steer_Servo_FL.pin1, MPU9250.pin2, LED_GND.pin1, LED_GND.pin2, LED_GND.pin3, LED_GND.pin4, Encoder_Power.pin3, Encoder_Power.pin4, SBC_Power.pin1, Switch.pin1, Steer_Servo_FR.pin1, Buzzer.2, Microphone_Power.pin2
  N1: Arduino_Nano_1.D2, RL_Encoder_1.pin1
  N2: Arduino_Nano_1.D3, RR_Encoder_1.pin1
  N3: Arduino_Nano_1.D5, Steer_Servo_RL.pin1
  N4: Arduino_Nano_1.D6, Steer_Servo_RR.pin1
  N5: Arduino_Nano_1.D7, RL_Encoder_2.pin1
  N6: Arduino_Nano_1.D8, RR_Encoder_2.pin1
  N7: Arduino_Nano_1.D9, Buzzer.1
  N8: Arduino_Nano_1.D10, Motor_Driver_Rear.PWMB
  N9: Arduino_Nano_1.D11/MOSI, Motor_Driver_Rear.PWMA
  VIN: Arduino_Nano_1.VIN, Steer_Servo_RR.pin2, Steer_Servo_RL.pin2, Motor_Driver_Rear.VCC, Motor_Driver_Rear.VM, Motor_Driver_Front.VCC, Motor_Driver_Front.VM, Arduino_Nano_2.VIN, Steer_Servo_FL.pin2, MPU9250.pin1, Encoder_Power.pin1, Encoder_Power.pin2, SBC_Power.pin2, Switch.pin2, Steer_Servo_FR.pin2, Microphone_Power.pin1
  N10: Arduino_Nano_1.A7, Microphone.pin2
  N11: Arduino_Nano_1.A6, Microphone.pin1
  N12: Arduino_Nano_1.A5, MPU9250.pin3
  N13: Arduino_Nano_1.A4, MPU9250.pin4
  N14: Arduino_Nano_1.A3, Motor_Driver_Rear.BIN2
  N15: Arduino_Nano_1.A2, Motor_Driver_Rear.BIN1
  N16: Arduino_Nano_1.A1, Motor_Driver_Rear.STBY
  N17: Arduino_Nano_1.A0, Motor_Driver_Rear.AIN1
  N18: Arduino_Nano_1.D13/SCK, Motor_Driver_Rear.AIN2
  N19: Motor_Driver_Rear.B01, Drive_Motor_RL.pin2
  N20: Motor_Driver_Rear.B02, Drive_Motor_RL.pin1
  N21: Motor_Driver_Rear.A02, Drive_Motor_RR.pin2
  N22: Motor_Driver_Rear.A01, Drive_Motor_RR.pin1
  N23: Motor_Driver_Front.B01, Drive_Motor_FR.pin2
  N24: Motor_Driver_Front.B02, Drive_Motor_FR.pin1
  N25: Motor_Driver_Front.A02, Drive_Motor_FL.pin2
  N26: Motor_Driver_Front.A01, Drive_Motor_FL.pin1
  N27: Motor_Driver_Front.PWMA, Arduino_Nano_2.D11/MOSI
  N28: Motor_Driver_Front.AIN2, Arduino_Nano_2.D13/SCK
  N29: Motor_Driver_Front.AIN1, Arduino_Nano_2.A0
  N30: Motor_Driver_Front.STBY, Arduino_Nano_2.A1
  N31: Motor_Driver_Front.BIN1, Arduino_Nano_2.A2
  N32: Motor_Driver_Front.BIN2, Arduino_Nano_2.A3
  N33: Motor_Driver_Front.PWMB, Arduino_Nano_2.D10
  N34: Arduino_Nano_2.D2, FL_Encoder_1.pin1
  N35: Arduino_Nano_2.D3, FR_Encoder_1.pin1
  N36: Arduino_Nano_2.D4, Reverse_Indicators.pin1, Reverse_Indicators.pin2
  N37: Arduino_Nano_2.D5, Steer_Servo_FL.pin3
  N38: Arduino_Nano_2.D6, Steer_Servo_FR.pin3
  N39: Arduino_Nano_2.D7, FL_Encoder_2.pin1
  N40: Arduino_Nano_2.D8, FR_Encoder_2.pin1
  N41: Arduino_Nano_2.D9, Taillights.pin1, Taillights.pin2
  N42: Arduino_Nano_2.A7, Right_Indicators.pin1, Right_Indicators.pin2
  N43: Arduino_Nano_2.A6, Left_Indicators.pin1, Left_Indicators.pin2
  N44: Arduino_Nano_2.A5, Headlights_(High_Beam).pin1, Headlights_(High_Beam).pin2
  N45: Arduino_Nano_2.A4, Headlights_(Low_Beam).pin1, Headlights_(Low_Beam).pin2

notes:
  A1
  A2
  E11
  E21
  E12
  E22
  L1
  L2
  L3
  L4
  L5
  S2
  S1
  E31
  E41
  E42
  E32
  S4
  S3
  M1
  M2
  M4
  M3
  D1
  D2
  IMU
  LED
  ENC
  SBC
  POW
  B1
  Q1
  MIC
